// Logisim project SymulatorProfesora.circ as structural Verilog: 1 circuit, main circuit main
module main (
  input  in_1,
  input  in_2
);

  wire clock_1_out, clock_2_out, comparator_1_eq, comparator_2_eq, controlled_buffer_1_out, keyboard_1_avail,
       main_1_output, main_3_done, not_1_out, or_1_out;
  wire [4:0] adder_1_out, counter_1_q, counter_2_q, register_2_q;
  wire [6:0] keyboard_1_data, main_2_out_4, register_1_q;
  wire [31:0] main_3_out_4, main_3_out_5, main_3_out_6, main_3_out_7, main_3_out_8, main_3_out_9,
       main_3_out_10, main_3_out_11, main_3_out_12, main_3_out_13, main_3_out_14, main_3_out_15,
       main_3_out_16, main_3_out_17, main_3_out_18, main_3_out_19, main_3_out_20, main_3_out_21,
       main_3_out_22, main_3_out_23, main_3_out_24, main_3_out_25, main_3_out_26, main_3_out_27,
       main_3_out_28, main_3_out_29, main_3_out_30, main_3_out_31, main_3_out_32, main_3_out_33,
       main_3_out_34, main_3_out_35, rom_1_data;

  Clock clock_1 (.out(clock_1_out));
  assign controlled_buffer_1_out = keyboard_1_avail ? clock_2_out : 1'bz;  // Controlled_Buffer controlled_buffer_1
  Keyboard keyboard_1 (
    .clk(controlled_buffer_1_out), .re(1'b1), .avail(keyboard_1_avail), .data(keyboard_1_data));  // open: clr
  Pull_Resistor pull_resistor_1 (.node(controlled_buffer_1_out));
  single_pulse_generator_main main_1 (.trigger(in_1), .\output (main_1_output), .clock(clock_1_out));
  Register #(.width(7)) register_1 (
    .D(keyboard_1_data), .Q(register_1_q), .clk(controlled_buffer_1_out), .clr(not_1_out));  // open: en
  not not_1 (not_1_out, clock_2_out);
  ROM_message_spitter_main main_2 (.clock(clock_1_out), .out_4(main_2_out_4), .reset(in_2), .trigger(main_1_output));
  Comparator #(.width(7), .mode("unsigned")) comparator_1 (
    .a(register_1_q), .b(7'b1100100), .eq(comparator_1_eq));  // open: gt, lt
  Comparator #(.width(7), .mode("unsigned")) comparator_2 (
    .a(register_1_q), .b(7'b1100001), .eq(comparator_2_eq));  // open: gt, lt
  or or_1 (or_1_out, comparator_1_eq, comparator_2_eq);
  Clock clock_2 (.out(clock_2_out));
  Counter #(.width(5), .max('h1b), .ongoal("stay")) counter_1 (
    .load(comparator_1_eq), .Q(counter_1_q), .clk(or_1_out));  // open: D, count, carry, clr
  Counter #(.width(5), .max('h1f)) counter_2 (.Q(counter_2_q), .clk(clock_2_out));  // open: load, D, count, carry, clr
  TTY tty_1 (.data(main_2_out_4), .clk(clock_1_out), .clr(main_1_output));  // open: we
  Register #(.width(5)) register_2 (.D(counter_1_q), .Q(register_2_q), .clk(main_3_done));  // open: en, clr
  Adder #(.width(5)) adder_1 (.a(register_2_q), .b(counter_2_q), .out(adder_1_out));  // open: cin, cout
  ROM #(.addrWidth(5), .dataWidth(32)) rom_1 (.addr(adder_1_out), .data(rom_1_data));  // open: sel
  DotMatrix #(.matrixcols(32), .matrixrows(32)) dotmatrix_1 (
    .col0(main_3_out_4), .col1(main_3_out_5), .col2(main_3_out_6), .col3(main_3_out_7), .col4(main_3_out_8),
    .col5(main_3_out_9), .col6(main_3_out_10), .col7(main_3_out_11), .col8(main_3_out_12),
    .col9(main_3_out_13), .col10(main_3_out_14), .col11(main_3_out_15), .col12(main_3_out_16),
    .col13(main_3_out_17), .col14(main_3_out_18), .col15(main_3_out_19), .col16(main_3_out_20),
    .col17(main_3_out_21), .col18(main_3_out_22), .col19(main_3_out_23), .col20(main_3_out_24),
    .col21(main_3_out_25), .col22(main_3_out_26), .col23(main_3_out_27), .col24(main_3_out_28),
    .col25(main_3_out_29), .col26(main_3_out_30), .col27(main_3_out_31), .col28(main_3_out_32),
    .col29(main_3_out_33), .col30(main_3_out_34), .col31(main_3_out_35));
  display_buffer_main main_3 (
    .Address(rom_1_data), .Select(counter_2_q), .out_4(main_3_out_4), .out_5(main_3_out_5),
    .out_6(main_3_out_6), .out_7(main_3_out_7), .out_8(main_3_out_8), .out_9(main_3_out_9),
    .out_10(main_3_out_10), .out_11(main_3_out_11), .out_12(main_3_out_12), .out_13(main_3_out_13),
    .out_14(main_3_out_14), .out_15(main_3_out_15), .out_16(main_3_out_16), .out_17(main_3_out_17),
    .out_18(main_3_out_18), .out_19(main_3_out_19), .out_20(main_3_out_20), .out_21(main_3_out_21),
    .out_22(main_3_out_22), .out_23(main_3_out_23), .out_24(main_3_out_24), .out_25(main_3_out_25),
    .out_26(main_3_out_26), .out_27(main_3_out_27), .out_28(main_3_out_28), .out_29(main_3_out_29),
    .out_30(main_3_out_30), .out_31(main_3_out_31), .out_32(main_3_out_32), .out_33(main_3_out_33),
    .out_34(main_3_out_34), .out_35(main_3_out_35), .Done(main_3_done));

  // Notes on the sheet:
  //   Zegar:szybko
  //   contents of rom_1 (hex, n*v repeats v):
  //   27*0 4 7 e 7 4
endmodule
